// Logisim project 7segmentDisplay.circ as structural Verilog: 8 circuits, main circuit main
module main (
  input  in_1,
  input  in_2,
  input  in_3
);

  wire circ0_1_out_4, circ1_1_out_4, circ2_1_out_3, circ3_1_out_4, circ4_1_out_4, circ5_1_out_4,
       circ6_1_out_4;

  circ0 circ0_1 (.A1(in_1), .B1(in_2), .C1(in_3), .out_4(circ0_1_out_4));
  circ1 circ1_1 (.A2(in_1), .B2(in_2), .C2(in_3), .out_4(circ1_1_out_4));
  circ2 circ2_1 (.B3(in_2), .C3(in_3), .out_3(circ2_1_out_3));
  circ3 circ3_1 (.A4(in_1), .B4(in_2), .C4(in_3), .out_4(circ3_1_out_4));
  circ4 circ4_1 (.A5(in_1), .B5(in_2), .C5(in_3), .out_4(circ4_1_out_4));
  circ5 circ5_1 (.A6(in_1), .B6(in_2), .C6(in_3), .out_4(circ5_1_out_4));
  circ6 circ6_1 (.A7(in_1), .B7(in_2), .C7(in_3), .out_4(circ6_1_out_4));
  _7_Segment_Display u_7_segment_display_1 (
    .g(circ6_1_out_4), .f(circ5_1_out_4), .a(circ0_1_out_4), .b(circ1_1_out_4), .e(circ4_1_out_4),
    .d(circ3_1_out_4), .c(circ2_1_out_3));  // open: dp
endmodule

module circ0 (
  input  A1,
  input  B1,
  input  C1,
  output out_4
);

  wire and_1_out, and_2_out, and_3_out, not_1_out, not_2_out, not_3_out, not_4_out, not_5_out;

  not not_1 (not_1_out, A1);
  not not_2 (not_2_out, A1);
  not not_3 (not_3_out, B1);
  not not_4 (not_4_out, C1);
  not not_5 (not_5_out, C1);
  and and_1 (and_1_out, not_1_out, B1, C1);
  and and_2 (and_2_out, not_2_out, not_3_out, not_4_out);
  and and_3 (and_3_out, A1, B1, not_5_out);
  or or_1 (out_4, and_1_out, and_2_out, and_3_out);
endmodule

module circ1 (
  input  A2,
  input  B2,
  input  C2,
  output out_4
);

  wire and_1_out, and_2_out, and_3_out, not_1_out, not_2_out, not_3_out, not_4_out;

  not not_1 (not_1_out, C2);
  not not_2 (not_2_out, A2);
  not not_3 (not_3_out, B2);
  not not_4 (not_4_out, C2);
  and and_1 (and_1_out, A2, not_1_out);
  and and_2 (and_2_out, not_2_out, B2, C2);
  and and_3 (and_3_out, not_3_out, not_4_out);
  or or_1 (out_4, and_1_out, and_2_out, and_3_out);
endmodule

module circ2 (
  input  B3,
  input  C3,
  output out_3
);

  wire not_1_out;

  not not_1 (not_1_out, C3);
  or or_1 (out_3, B3, not_1_out);
endmodule

module circ3 (
  input  A4,
  input  B4,
  input  C4,
  output out_4
);

  wire and_1_out, and_2_out, not_1_out, not_2_out, not_3_out;

  not not_1 (not_1_out, A4);
  not not_2 (not_2_out, B4);
  not not_3 (not_3_out, C4);
  and and_1 (and_1_out, not_1_out, B4);
  and and_2 (and_2_out, not_2_out, not_3_out);
  or or_1 (out_4, and_1_out, and_2_out);
endmodule

module circ4 (
  input  A5,
  input  B5,
  input  C5,
  output out_4
);

  wire not_1_out;

  not not_1 (not_1_out, C5);
  or or_1 (out_4, A5, B5, not_1_out);
endmodule

module circ5 (
  input  A6,
  input  B6,
  input  C6,
  output out_4
);

  wire and_1_out, and_2_out, and_3_out, and_4_out, not_1_out, not_2_out, not_3_out, not_4_out, not_5_out;

  not not_1 (not_1_out, B6);
  not not_2 (not_2_out, A6);
  not not_3 (not_3_out, A6);
  not not_4 (not_4_out, C6);
  not not_5 (not_5_out, C6);
  and and_1 (and_1_out, A6, not_1_out, C6);
  and and_2 (and_2_out, not_2_out, B6);
  and and_3 (and_3_out, not_3_out, not_4_out);
  and and_4 (and_4_out, B6, not_5_out);
  or or_1 (out_4, and_1_out, and_2_out, and_3_out, and_4_out);
endmodule

module circ6 (
  input  A7,
  input  B7,
  input  C7,
  output out_4
);

  wire and_1_out, and_2_out, not_1_out;

  not not_1 (not_1_out, C7);
  and and_1 (and_1_out, A7, B7);
  and and_2 (and_2_out, B7, not_1_out);
  or or_1 (out_4, and_1_out, and_2_out);
endmodule
