// Logisim project goldenEyePenFiniteStateMachines.circ as structural Verilog: 4 circuits, main circuit srlatch
module srlatch (
  input  C,
  input  S,
  input  R,
  output notq,
  output q
);

  wire and_1_out, and_2_out;

  and and_1 (and_1_out, S, C);
  and and_2 (and_2_out, C, R);
  nor nor_1 (notq, and_1_out, q);
  nor nor_2 (q, notq, and_2_out);
endmodule

module dlatch (
  input  d,
  input  C,
  output notq,
  output q
);

  wire not_1_out;

  not not_1 (not_1_out, d);
  srlatch srlatch_1 (.C(C), .S(d), .R(not_1_out), .notq(notq), .q(q));
endmodule

module posdflipflop (
  input  D,
  input  C,
  output notQ,
  output Q
);

  wire dlatch_1_q, not_1_out, not_2_out;

  not not_1 (not_1_out, C);
  not not_2 (not_2_out, not_1_out);
  dlatch dlatch_1 (.d(D), .C(not_1_out), .q(dlatch_1_q));  // open: notq
  dlatch dlatch_2 (.d(dlatch_1_q), .C(not_2_out), .notq(notQ), .q(Q));
endmodule

module pen (
  input  reset,
  output out_2
);

  wire button_1_out, F0_q, F1_q, F1F0_out, F2_q, F2F1_out, F2NotF0_out, F3_q, ForF0_out, ForF1_out,
       ForF2_out, ForF3_out, not_1_out, not_2_out, not_3_out, not_4_out, NotF1F0_out, NotF3F1NotF0_out,
       NotF3F2_out, NotF3F2NotF1_out, NotF3NotF1NotF0_out, NotF3NotF2F1_out;

  Button button_1 (.out(button_1_out));
  D_Flip_Flop F0 (.D(ForF0_out), .clk(button_1_out), .Q(F0_q), .reset(reset));  // open: Qn, preset
  D_Flip_Flop F1 (.D(ForF1_out), .clk(button_1_out), .Q(F1_q), .reset(reset));  // open: Qn, preset
  D_Flip_Flop F2 (.D(ForF2_out), .clk(button_1_out), .Q(F2_q), .reset(reset));  // open: Qn, preset
  D_Flip_Flop F3 (.D(ForF3_out), .clk(button_1_out), .Q(F3_q), .reset(reset));  // open: Qn, preset
  and ForF3 (ForF3_out, not_1_out, F2_q);
  not not_1 (not_1_out, F0_q);
  not not_2 (not_2_out, F1_q);
  not not_3 (not_3_out, F3_q);
  and NotF3NotF1NotF0 (NotF3NotF1NotF0_out, not_3_out, not_2_out, not_1_out);
  and NotF1F0 (NotF1F0_out, F0_q, not_2_out);
  and F1F0 (F1F0_out, F0_q, F1_q);
  and F2F1 (F2F1_out, F1_q, F2_q);
  and NotF3F2 (NotF3F2_out, not_3_out, F2_q);
  and NotF3F1NotF0 (NotF3F1NotF0_out, not_1_out, F1_q, not_3_out);
  not not_4 (not_4_out, F2_q);
  and NotF3NotF2F1 (NotF3NotF2F1_out, F1_q, not_4_out, not_3_out);
  and NotF3F2NotF1 (NotF3F2NotF1_out, NotF3F2_out, not_2_out);
  or ForF2 (ForF2_out, F1F0_out, F2F1_out, NotF3F2_out);
  or ForF1 (ForF1_out, NotF3F1NotF0_out, NotF1F0_out, NotF3F2_out);
  and F2NotF0 (F2NotF0_out, not_1_out, F2_q);
  or ForF0 (ForF0_out, NotF3NotF2F1_out, NotF3F2NotF1_out, NotF3NotF1NotF0_out);
  or or_1 (out_2, F2NotF0_out, F2F1_out);
endmodule
