// Logisim project latchesFlipflops.circ as structural Verilog: 3 circuits, main circuit srlatch
module srlatch (
  input  C,
  input  S,
  input  R,
  output notq,
  output q
);

  wire and_1_out, and_2_out;

  and and_1 (and_1_out, S, C);
  and and_2 (and_2_out, C, R);
  nor nor_1 (notq, and_1_out, q);
  nor nor_2 (q, notq, and_2_out);
endmodule

module dlatch (
  input  d,
  input  C,
  output notq,
  output q
);

  wire not_1_out;

  not not_1 (not_1_out, d);
  srlatch srlatch_1 (.C(C), .S(d), .R(not_1_out), .notq(notq), .q(q));
endmodule

module posdflipflop (
  input  D,
  input  C,
  output notQ,
  output Q
);

  wire dlatch_1_q, not_1_out, not_2_out;

  not not_1 (not_1_out, C);
  not not_2 (not_2_out, not_1_out);
  dlatch dlatch_1 (.d(D), .C(not_1_out), .q(dlatch_1_q));  // open: notq
  dlatch dlatch_2 (.d(dlatch_1_q), .C(not_2_out), .notq(notQ), .q(Q));
endmodule
