// Logisim project muxdemux.circ as structural Verilog: 5 circuits, main circuit mux2to1
module mux2to1 (
  input  x,
  input  s,
  input  y,
  output m
);

  wire and_1_out, and_2_out, not_1_out;

  not not_1 (not_1_out, s);
  and and_1 (and_1_out, x, not_1_out);
  and and_2 (and_2_out, s, y);
  or or_1 (m, and_1_out, and_2_out);
endmodule

module demux1to2 (
  input  m,
  input  s,
  output x,
  output y
);

  wire not_1_out;

  not not_1 (not_1_out, s);
  and and_1 (x, m, not_1_out);
  and and_2 (y, s, m);
endmodule

module mux6to1 (
  input  i0,
  input  i1,
  input  i2,
  input  i3,
  input  i4,
  input  i5,
  input  s0,
  input  s1,
  input  s2,
  output out_10
);

  wire mux2to1_1_m, mux2to1_2_m, mux2to1_3_m, mux2to1_4_m, mux2to1_5_m;

  mux2to1 mux2to1_1 (.x(i0), .s(s0), .y(i1), .m(mux2to1_1_m));
  mux2to1 mux2to1_2 (.x(i2), .s(s0), .y(i3), .m(mux2to1_2_m));
  mux2to1 mux2to1_3 (.x(i4), .s(s0), .y(i5), .m(mux2to1_3_m));
  mux2to1 mux2to1_4 (.x(mux2to1_1_m), .s(s1), .y(mux2to1_2_m), .m(mux2to1_4_m));
  mux2to1 mux2to1_5 (.x(mux2to1_3_m), .s(s1), .m(mux2to1_5_m));  // open: y
  mux2to1 mux2to1_6 (.x(mux2to1_4_m), .s(s2), .y(mux2to1_5_m), .m(out_10));
endmodule

module demux6to1 (
  input  i,
  input  s2,
  input  s1,
  input  s0,
  output o1,
  output o2,
  output o3,
  output o4,
  output o5,
  output o6
);

  wire demux1to2_1_x, demux1to2_1_y, demux1to2_2_x, demux1to2_2_y, demux1to2_3_x;

  demux1to2 demux1to2_1 (.m(i), .s(s2), .x(demux1to2_1_x), .y(demux1to2_1_y));
  demux1to2 demux1to2_2 (.m(demux1to2_1_x), .s(s1), .x(demux1to2_2_x), .y(demux1to2_2_y));
  demux1to2 demux1to2_3 (.m(demux1to2_1_y), .s(s1), .x(demux1to2_3_x));  // open: y
  demux1to2 demux1to2_4 (.m(demux1to2_2_x), .s(s0), .x(o1), .y(o2));
  demux1to2 demux1to2_5 (.m(demux1to2_2_y), .s(s0), .x(o3), .y(o4));
  demux1to2 demux1to2_6 (.m(demux1to2_3_x), .s(s0), .x(o5), .y(o6));
endmodule

module temp (
  input  in_1,
  input  in_2,
  input  in_3,
  input  in_4
);

  wire mux6to1_1_out_10, mux6to1_2_out_10;

  mux6to1 mux6to1_1 (.s0(in_1), .s1(in_2), .s2(in_3), .out_10(mux6to1_1_out_10));  // open: i0, i1, i2, i3, i4, i5
  mux6to1 mux6to1_2 (.out_10(mux6to1_2_out_10));  // open: i0, i1, i2, i3, i4, i5, s0, s1, s2
  mux2to1 mux2to1_1 (.x(mux6to1_1_out_10), .s(in_4), .y(mux6to1_2_out_10));  // open: m
endmodule
