// Logisim project registerFiles.circ as structural Verilog: 2 circuits, main circuit main
module main (
  input  [3:0] data,
  input  WE,
  input  [1:0] write_select,
  input  [1:0] read_select,
  output [3:0] out_5
);

  wire Clock_out, Reset_out;

  Button Clock (.out(Clock_out));
  Button Reset (.out(Reset_out));
  RegisterFile registerfile_1 (
    .data(data), .WE(WE), .write_select(write_select), .read_select(read_select), .Clock(Clock_out),
    .Reset(Reset_out), .Q(out_5));
endmodule

module RegisterFile (
  input  [3:0] data,
  input  WE,
  input  [1:0] write_select,
  input  [1:0] read_select,
  input  Clock,
  input  Reset,
  output [3:0] Q
);

  wire demultiplexer_1_out0, demultiplexer_1_out1, demultiplexer_1_out2, demultiplexer_1_out3;
  wire [3:0] Reg0_q, Reg1_q, Reg2_q, Reg3_q;

  Demultiplexer #(.enable("false"), .select(2)) demultiplexer_1 (
    .out0(demultiplexer_1_out0), .out1(demultiplexer_1_out1), .out2(demultiplexer_1_out2),
    .out3(demultiplexer_1_out3), .in(WE), .sel(write_select));
  Register #(.width(4)) Reg0 (.D(data), .en(demultiplexer_1_out0), .clk(Clock), .Q(Reg0_q), .clr(Reset));
  Register #(.width(4)) Reg1 (.D(data), .en(demultiplexer_1_out1), .clk(Clock), .Q(Reg1_q), .clr(Reset));
  Register #(.width(4)) Reg2 (.D(data), .en(demultiplexer_1_out2), .clk(Clock), .Q(Reg2_q), .clr(Reset));
  Register #(.width(4)) Reg3 (.D(data), .en(demultiplexer_1_out3), .clk(Clock), .Q(Reg3_q), .clr(Reset));
  Multiplexer #(.enable("false"), .select(2), .width(4)) multiplexer_1 (
    .in0(Reg0_q), .in1(Reg1_q), .in2(Reg2_q), .in3(Reg3_q), .out(Q), .sel(read_select));
endmodule
